// Logisim project 3display.circ as structural Verilog: 3 circuits, main circuit main
module main (
  input  in_1,
  input  in_2,
  input  in_3,
  input  in_4,
  input  [7:0] in_5
);

  wire add3_1_out_5, add3_1_out_6, add3_1_out_7, add3_1_out_8, add3_2_out_5, add3_2_out_6, add3_2_out_7,
       add3_2_out_8, add3_3_out_5, add3_3_out_6, add3_3_out_7, add3_3_out_8, add3_4_out_5, add3_4_out_6,
       add3_4_out_7, add3_4_out_8, add3_5_out_5, add3_5_out_6, add3_5_out_7, add3_5_out_8, add3_6_out_5,
       add3_6_out_6, add3_6_out_7, add3_6_out_8, add3_7_out_5, add3_7_out_6, add3_7_out_7, add3_7_out_8,
       clock_1_out, display_1_out_6, display_1_out_7, display_1_out_8, display_1_out_9, display_1_out_10,
       display_1_out_11, display_1_out_12, display_2_out_6, display_2_out_7, display_2_out_8,
       display_2_out_9, display_2_out_10, display_2_out_11, display_2_out_12, display_3_out_6,
       display_3_out_7, display_3_out_8, display_3_out_9, display_3_out_10, display_3_out_11,
       display_3_out_12;

  add3 add3_1 (
    .in_1(in_4), .in_2(in_5[7]), .in_3(in_5[6]), .in_4(in_5[5]), .out_5(add3_1_out_5), .out_6(add3_1_out_6),
    .out_7(add3_1_out_7), .out_8(add3_1_out_8));
  Clock clock_1 (.out(clock_1_out));
  add3 add3_2 (
    .in_1(add3_1_out_6), .in_2(add3_1_out_7), .in_3(add3_1_out_8), .in_4(in_5[4]), .out_5(add3_2_out_5),
    .out_6(add3_2_out_6), .out_7(add3_2_out_7), .out_8(add3_2_out_8));
  add3 add3_3 (
    .in_1(add3_2_out_6), .in_2(add3_2_out_7), .in_3(add3_2_out_8), .in_4(in_5[3]), .out_5(add3_3_out_5),
    .out_6(add3_3_out_6), .out_7(add3_3_out_7), .out_8(add3_3_out_8));
  add3 add3_4 (
    .in_1(add3_3_out_6), .in_2(add3_3_out_7), .in_3(add3_3_out_8), .in_4(in_5[2]), .out_5(add3_4_out_5),
    .out_6(add3_4_out_6), .out_7(add3_4_out_7), .out_8(add3_4_out_8));
  add3 add3_5 (
    .in_1(in_1), .in_2(add3_1_out_5), .in_3(add3_2_out_5), .in_4(add3_3_out_5), .out_5(add3_5_out_5),
    .out_6(add3_5_out_6), .out_7(add3_5_out_7), .out_8(add3_5_out_8));
  add3 add3_6 (
    .in_1(add3_4_out_6), .in_2(add3_4_out_7), .in_3(add3_4_out_8), .in_4(in_5[1]), .out_5(add3_6_out_5),
    .out_6(add3_6_out_6), .out_7(add3_6_out_7), .out_8(add3_6_out_8));
  add3 add3_7 (
    .in_1(add3_5_out_6), .in_2(add3_5_out_7), .in_3(add3_5_out_8), .in_4(add3_4_out_5), .out_5(add3_7_out_5),
    .out_6(add3_7_out_6), .out_7(add3_7_out_7), .out_8(add3_7_out_8));
  display display_1 (
    .lsb(in_2), .in_2(in_3), .in_3(add3_5_out_5), .msb(add3_7_out_5), .in_5(clock_1_out),
    .out_6(display_1_out_6), .out_7(display_1_out_7), .out_8(display_1_out_8), .out_9(display_1_out_9),
    .out_10(display_1_out_10), .out_11(display_1_out_11), .out_12(display_1_out_12));
  display display_2 (
    .lsb(add3_7_out_6), .in_2(add3_7_out_7), .in_3(add3_7_out_8), .msb(add3_6_out_5), .in_5(clock_1_out),
    .out_6(display_2_out_6), .out_7(display_2_out_7), .out_8(display_2_out_8), .out_9(display_2_out_9),
    .out_10(display_2_out_10), .out_11(display_2_out_11), .out_12(display_2_out_12));
  display display_3 (
    .lsb(in_5[0]), .in_2(add3_6_out_8), .in_3(add3_6_out_7), .msb(add3_6_out_6), .in_5(clock_1_out),
    .out_6(display_3_out_6), .out_7(display_3_out_7), .out_8(display_3_out_8), .out_9(display_3_out_9),
    .out_10(display_3_out_10), .out_11(display_3_out_11), .out_12(display_3_out_12));
  _7_Segment_Display u_7_segment_display_1 (
    .g(display_1_out_6), .f(display_1_out_7), .a(display_1_out_8), .b(display_1_out_9), .e(display_1_out_10),
    .d(display_1_out_11), .c(display_1_out_12));  // open: dp
  _7_Segment_Display u_7_segment_display_2 (
    .g(display_2_out_6), .f(display_2_out_7), .a(display_2_out_8), .b(display_2_out_9), .e(display_2_out_10),
    .d(display_2_out_11), .c(display_2_out_12));  // open: dp
  _7_Segment_Display u_7_segment_display_3 (
    .g(display_3_out_6), .f(display_3_out_7), .a(display_3_out_8), .b(display_3_out_9), .e(display_3_out_10),
    .d(display_3_out_11), .c(display_3_out_12));  // open: dp

  // Notes on the sheet:
  //   hundreds
  //   tens
  //   ones
endmodule

module add3 (
  input  in_1,
  input  in_2,
  input  in_3,
  input  in_4,
  output out_5,
  output out_6,
  output out_7,
  output out_8
);

  wire a5_out, a6_out, a7_out, a8_out, a9_out, a10_out, a11_out, a12_out, a13_out, a14_out, a15_out,
       and_5_out, and_6_out, and_7_out, and_8_out, and_9_out, and_10_out, and_11_out, and_12_out, not_1_out,
       not_2_out, not_3_out, not_4_out, not_6_out, or_1_out;
  wire [3:0] adder_1_out, and_1_out;
  wire [3:3] not_5_out;

  not not_1 (not_1_out, in_4);
  not not_2 (not_2_out, in_3);
  not not_3 (not_3_out, in_2);
  not not_4 (not_4_out, in_1);
  and a15 (a15_out, in_1, in_2, in_3, in_4);
  and a14 (a14_out, in_1, in_3, not_1_out);
  and a13 (a13_out, in_1, in_2, not_2_out, in_4);
  and a12 (a12_out, in_1, in_2, not_2_out, not_1_out);
  and a11 (a11_out, in_1, not_3_out, in_3, in_4);
  and a10 (a10_out, in_1, not_3_out, in_3, not_1_out);
  and a9 (a9_out, in_1, not_3_out, not_2_out, in_4);
  and a8 (a8_out, in_1, not_3_out, not_2_out, not_1_out);
  and a7 (a7_out, not_4_out, in_2, in_3, in_4);
  and a6 (a6_out, not_4_out, in_2, in_3, not_1_out);
  and a5 (a5_out, not_4_out, in_2, not_2_out, in_4);
  or or_1 (or_1_out, a14_out, a13_out, a12_out, a11_out, a10_out, a15_out, a9_out, a8_out, a7_out, a6_out, a5_out);
  and and_1 (and_1_out[0], in_1, or_1_out);
  and and_2 (and_1_out[1], in_2, or_1_out);
  and and_3 (and_1_out[2], in_3, or_1_out);
  and and_4 (and_1_out[3], in_4, or_1_out);
  Adder #(.width(4)) adder_1 (.a(and_1_out), .b({{2{not_5_out[3]}}, 2'b11}), .out(adder_1_out));  // open: cin, cout
  not not_5 (not_5_out[3], 1'b1);
  and and_5 (and_5_out, adder_1_out[3], or_1_out);
  and and_6 (and_6_out, adder_1_out[2], or_1_out);
  and and_7 (and_7_out, adder_1_out[1], or_1_out);
  and and_8 (and_8_out, adder_1_out[0], or_1_out);
  and and_9 (and_9_out, in_1, not_6_out);
  and and_10 (and_10_out, in_2, not_6_out);
  and and_11 (and_11_out, in_3, not_6_out);
  and and_12 (and_12_out, in_4, not_6_out);
  not not_6 (not_6_out, or_1_out);
  or or_2 (out_5, and_9_out, and_5_out);
  or or_3 (out_6, and_10_out, and_6_out);
  or or_4 (out_7, and_11_out, and_7_out);
  or or_5 (out_8, and_12_out, and_8_out);

  // Notes on the sheet:
  //   add 3
endmodule

module display (
  input  lsb,
  input  in_2,
  input  in_3,
  input  msb,
  input  in_5,
  output out_6,
  output out_7,
  output out_8,
  output out_9,
  output out_10,
  output out_11,
  output out_12
);

  wire and_1_out, and_2_out, and_3_out, and_4_out, and_5_out, and_6_out, and_7_out, and_8_out, and_9_out,
       and_10_out, and_11_out, and_12_out, and_13_out, and_14_out, and_15_out, and_16_out, and_17_out,
       buffer_1_out, buffer_2_out, nand_1_out, nand_2_out, nand_3_out, nand_4_out, not_1_out, not_2_out,
       not_3_out, not_4_out;

  not not_1 (not_1_out, lsb);
  not not_2 (not_2_out, in_2);
  not not_3 (not_3_out, in_3);
  not not_4 (not_4_out, msb);
  buf buffer_1 (buffer_1_out, in_5);
  nand nand_1 (nand_1_out, not_1_out, buffer_1_out);
  nand nand_2 (nand_2_out, not_2_out, buffer_1_out);
  nand nand_3 (nand_3_out, not_3_out, buffer_1_out);
  nand nand_4 (nand_4_out, not_4_out, buffer_1_out);
  and and_1 (and_1_out, nand_2_out, nand_4_out);
  and and_2 (and_2_out, not_1_out, nand_3_out);
  and and_3 (and_3_out, nand_1_out, not_2_out, not_3_out, not_4_out);
  and and_4 (and_4_out, nand_2_out, nand_4_out);
  and and_5 (and_5_out, nand_1_out, not_2_out, nand_3_out);
  and and_6 (and_6_out, not_1_out, nand_2_out, nand_3_out);
  and and_7 (and_7_out, nand_3_out, nand_4_out);
  and and_8 (and_8_out, not_1_out, nand_2_out, not_3_out);
  and and_9 (and_9_out, nand_1_out, not_2_out, not_3_out);
  and and_10 (and_10_out, not_1_out, not_2_out, nand_3_out);
  and and_11 (and_11_out, nand_1_out, nand_2_out, nand_3_out);
  buf buffer_2 (buffer_2_out, nand_1_out);
  and and_12 (and_12_out, not_2_out, nand_3_out);
  and and_13 (and_13_out, nand_1_out, nand_2_out);
  and and_14 (and_14_out, nand_2_out, not_3_out);
  and and_15 (and_15_out, nand_1_out, not_3_out, not_4_out);
  and and_16 (and_16_out, nand_1_out, nand_2_out, nand_3_out);
  and and_17 (and_17_out, not_2_out, not_3_out, not_4_out);
  nor nor_1 (out_8, and_1_out, and_2_out, and_3_out);
  nor nor_2 (out_9, and_4_out, and_5_out, and_6_out);
  nor nor_3 (out_12, and_7_out, and_8_out);
  nor nor_4 (out_11, and_9_out, and_10_out, and_11_out);
  nor nor_5 (out_10, buffer_2_out, and_12_out);
  nor nor_6 (out_7, and_13_out, and_14_out, and_15_out);
  nor nor_7 (out_6, and_16_out, and_17_out);

  // Notes on the sheet:
  //   (Logic 0 Blanks the display)
  //   BCD to 7-Segment Decoder Simulation
  //   (Based on 74HC49)
  //   www.learnabout-electronics.org
endmodule
