// Logisim project Four_Bits_Add_Sub.circ as structural Verilog: 5 circuits, main circuit Add_Sub_4Bits
module Add_Sub_4Bits (
  input  [3:0] A,
  input  [3:0] B,
  input  Add_Sub,
  output Zero,
  output Overflow,
  output [3:0] R
);

  wire add_1bit_1_cout, add_1bit_2_cout, halfadder_1bit_1_carry_bit, multiplexer_2scomplement_1_aout,
       multiplexer_2scomplement_1_bout, multiplexer_2scomplement_1_cout, multiplexer_2scomplement_1_dout,
       not_1_out;

  // Probe on A
  // Probe on B
  nor nor_1 (Zero, B[0], B[1], B[2], B[3], A[0], A[1], A[2], A[3]);
  not not_1 (not_1_out, Add_Sub);
  Multiplexer_2scomplement multiplexer_2scomplement_1 (
    .Bout(multiplexer_2scomplement_1_bout), .Ain(B[0]), .Cin(B[2]), .Din(B[3]), .Invert(not_1_out),
    .Aout(multiplexer_2scomplement_1_aout), .Bin(B[1]), .Cout(multiplexer_2scomplement_1_cout),
    .Dout(multiplexer_2scomplement_1_dout));
  HalfAdder_1bit halfadder_1bit_1 (
    .A(A[0]), .B(multiplexer_2scomplement_1_aout), .Sum_Bit(R[0]), .Carry_Bit(halfadder_1bit_1_carry_bit));
  // Probe on R
  Add_1Bit add_1bit_1 (
    .Sum(R[1]), .A(A[1]), .B(multiplexer_2scomplement_1_bout), .Cout(add_1bit_1_cout),
    .Cin(halfadder_1bit_1_carry_bit));
  Add_1Bit add_1bit_2 (
    .Sum(R[2]), .A(A[2]), .B(multiplexer_2scomplement_1_cout), .Cout(add_1bit_2_cout), .Cin(add_1bit_1_cout));
  Add_1Bit add_1bit_3 (
    .Sum(R[3]), .A(A[3]), .B(multiplexer_2scomplement_1_dout), .Cout(Overflow), .Cin(add_1bit_2_cout));

  // Notes on the sheet:
  //   Etienne Guillot-Marquet 260629183
  //   MAKE SURE THAT YOU OPENED THIS PROJECT IN "LOGISIM-EVOLUTION"
  //   YOU CAN FIND "LOGISIM-EVOLUTION" PRORAM IN THE ASSIGNMENT'S FOLDER
  //   DO NOT USE "LOGISIM" VERSION TO SOLVE THIS ASSIGNMENT!
endmodule

module Add_1Bit (
  input  Cin,
  input  A,
  input  B,
  output Sum,
  output Cout
);

  wire halfadder_1bit_1_carry_bit, halfadder_1bit_1_sum_bit, halfadder_1bit_2_carry_bit;

  HalfAdder_1bit halfadder_1bit_1 (
    .A(A), .B(B), .Sum_Bit(halfadder_1bit_1_sum_bit), .Carry_Bit(halfadder_1bit_1_carry_bit));
  HalfAdder_1bit halfadder_1bit_2 (
    .A(Cin), .B(halfadder_1bit_1_sum_bit), .Sum_Bit(Sum), .Carry_Bit(halfadder_1bit_2_carry_bit));
  or or_1 (Cout, halfadder_1bit_2_carry_bit, halfadder_1bit_1_carry_bit);

  // Notes on the sheet:
  //   Etienne Guillot-Marquet 260629183
  //   MAKE SURE THAT YOU OPENED THIS PROJECT IN "LOGISIM-EVOLUTION"
  //   YOU CAN FIND "LOGISIM-EVOLUTION" PRORAM IN THE ASSIGNMENT'S FOLDER
  //   DO NOT USE "LOGISIM" VERSION TO SOLVE THIS ASSIGNMENT!
endmodule

module HalfAdder_1bit (
  input  A,
  input  B,
  output Sum_Bit,
  output Carry_Bit
);

  xor xor_1 (Sum_Bit, A, B);
  and and_1 (Carry_Bit, A, B);
endmodule

module Multiplexer_2scomplement (
  input  Invert,
  input  Ain,
  input  Bin,
  input  Cin,
  input  Din,
  output Aout,
  output Bout,
  output Cout,
  output Dout
);

  wire add_1bit_1_cout, add_1bit_1_sum, add_1bit_2_cout, add_1bit_2_sum, add_1bit_3_sum, and_1_out,
       and_2_out, and_3_out, and_4_out, and_5_out, and_6_out, and_7_out, and_8_out,
       halfadder_1bit_1_carry_bit, halfadder_1bit_1_sum_bit, not_1_out, not_2_out, not_3_out, not_4_out,
       not_5_out;

  not not_1 (not_1_out, Din);
  not not_2 (not_2_out, Cin);
  not not_3 (not_3_out, Ain);
  not not_4 (not_4_out, Invert);
  not not_5 (not_5_out, Bin);
  and and_1 (and_1_out, Ain, Invert);
  and and_2 (and_2_out, Bin, Invert);
  and and_3 (and_3_out, Cin, Invert);
  and and_4 (and_4_out, Din, Invert);
  HalfAdder_1bit halfadder_1bit_1 (
    .A(not_3_out), .B(1'b1), .Sum_Bit(halfadder_1bit_1_sum_bit), .Carry_Bit(halfadder_1bit_1_carry_bit));
  Add_1Bit add_1bit_1 (
    .Sum(add_1bit_1_sum), .A(not_5_out), .Cout(add_1bit_1_cout), .Cin(halfadder_1bit_1_carry_bit));  // open: B
  Add_1Bit add_1bit_2 (.Sum(add_1bit_2_sum), .A(not_2_out), .Cout(add_1bit_2_cout), .Cin(add_1bit_1_cout));  // open: B
  Add_1Bit add_1bit_3 (.Sum(add_1bit_3_sum), .A(not_1_out), .Cin(add_1bit_2_cout));  // open: B, Cout
  and and_5 (and_5_out, not_4_out, halfadder_1bit_1_sum_bit);
  and and_6 (and_6_out, not_4_out, add_1bit_1_sum);
  and and_7 (and_7_out, not_4_out, add_1bit_2_sum);
  and and_8 (and_8_out, not_4_out, add_1bit_3_sum);
  or or_1 (Aout, and_1_out, and_5_out);
  or or_2 (Bout, and_2_out, and_6_out);
  or or_3 (Cout, and_3_out, and_7_out);
  or or_4 (Dout, and_4_out, and_8_out);
endmodule

module Adder_4bits (
  input  in_1,
  input  in_2,
  input  in_3,
  input  in_4,
  output out_5,
  output out_6,
  output out_7,
  output out_8
);

  wire add_1bit_1_cout, add_1bit_2_cout, halfadder_1bit_1_carry_bit;

  HalfAdder_1bit halfadder_1bit_1 (.A(in_1), .B(1'b1), .Sum_Bit(out_5), .Carry_Bit(halfadder_1bit_1_carry_bit));
  Add_1Bit add_1bit_1 (.Sum(out_6), .A(in_2), .Cout(add_1bit_1_cout), .Cin(halfadder_1bit_1_carry_bit));  // open: B
  Add_1Bit add_1bit_2 (.Sum(out_7), .A(in_3), .Cout(add_1bit_2_cout), .Cin(add_1bit_1_cout));  // open: B
  Add_1Bit add_1bit_3 (.Sum(out_8), .A(in_4), .Cin(add_1bit_2_cout));  // open: B, Cout
endmodule
