// Logisim project alu.circ as structural Verilog: 6 circuits, main circuit mainALU
module mainALU (
  input  addOrSub,
  input  [7:0] A,
  input  [7:0] B,
  input  andOr,
  input  mathOrLogic,
  output Carry,
  output Overflow,
  output Zero,
  output Negative,
  output [7:0] Result
);

  wire [7:0] Adder_Subtractor_result, andalu_1_result, multiplexer_1_out, oralu_1_result;

  adderSubtractorALU Adder_Subtractor (
    .A(A), .B(B), .AddSubControl(addOrSub), .Result(Adder_Subtractor_result), .Carry(Carry),
    .Overflow(Overflow));
  AndALU andalu_1 (.A(A), .B(B), .Result(andalu_1_result));
  OrALU oralu_1 (.A(A), .B(B), .Result(oralu_1_result));
  Multiplexer #(.width(8), .enable("false")) multiplexer_1 (
    .in0(andalu_1_result), .in1(oralu_1_result), .out(multiplexer_1_out), .sel(andOr));
  Multiplexer #(.width(8), .enable("false")) multiplexer_2 (
    .in0(Adder_Subtractor_result), .in1(multiplexer_1_out), .out({Negative, Result[6:0]}), .sel(mathOrLogic));
  nor nor_1 (Zero, Result[0], Result[1], Result[2], Result[3], Result[4], Result[5], Result[6], Negative);

  assign Result[7] = Negative;
endmodule

module fullAdderALU (
  input  CarryIn,
  input  A,
  input  B,
  output Result,
  output CarryOut
);

  wire and_1_out, and_2_out, xor_1_out;

  and and_1 (and_1_out, A, B);
  xor xor_1 (xor_1_out, A, B);
  xor xor_2 (Result, CarryIn, xor_1_out);
  and and_2 (and_2_out, xor_1_out, CarryIn);
  or or_1 (CarryOut, and_2_out, and_1_out);
endmodule

module adderALU (
  input  in_1,
  input  [7:0] A,
  input  [7:0] B,
  output [7:0] Result,
  output Overflow
);

  wire fulladderalu_1_carryout, fulladderalu_2_carryout, fulladderalu_3_carryout, fulladderalu_4_carryout,
       fulladderalu_5_carryout, fulladderalu_6_carryout, fulladderalu_7_carryout;

  fullAdderALU fulladderalu_1 (
    .CarryIn(in_1), .A(A[0]), .B(B[0]), .Result(Result[0]), .CarryOut(fulladderalu_1_carryout));
  fullAdderALU fulladderalu_2 (
    .CarryIn(fulladderalu_1_carryout), .A(A[1]), .B(B[1]), .Result(Result[1]),
    .CarryOut(fulladderalu_2_carryout));
  fullAdderALU fulladderalu_3 (
    .CarryIn(fulladderalu_2_carryout), .A(A[2]), .B(B[2]), .Result(Result[2]),
    .CarryOut(fulladderalu_3_carryout));
  fullAdderALU fulladderalu_4 (
    .CarryIn(fulladderalu_3_carryout), .A(A[3]), .B(B[3]), .Result(Result[3]),
    .CarryOut(fulladderalu_4_carryout));
  fullAdderALU fulladderalu_5 (
    .CarryIn(fulladderalu_4_carryout), .A(A[4]), .B(B[4]), .Result(Result[4]),
    .CarryOut(fulladderalu_5_carryout));
  fullAdderALU fulladderalu_6 (
    .CarryIn(fulladderalu_5_carryout), .A(A[5]), .B(B[5]), .Result(Result[5]),
    .CarryOut(fulladderalu_6_carryout));
  fullAdderALU fulladderalu_7 (
    .CarryIn(fulladderalu_6_carryout), .A(A[6]), .B(B[6]), .Result(Result[6]),
    .CarryOut(fulladderalu_7_carryout));
  fullAdderALU fulladderalu_8 (
    .CarryIn(fulladderalu_7_carryout), .A(A[7]), .B(B[7]), .Result(Result[7]), .CarryOut(Overflow));
endmodule

module adderSubtractorALU (
  input  AddSubControl,
  input  [7:0] A,
  input  [7:0] B,
  output [7:0] Result,
  output Carry,
  output Overflow
);

  wire and_1_out, and_2_out, fulladderalu_1_carryout, fulladderalu_2_carryout, fulladderalu_3_carryout,
       fulladderalu_4_carryout, fulladderalu_5_carryout, fulladderalu_6_carryout, fulladderalu_7_carryout,
       not_1_out, not_2_out, not_3_out, xor_1_out, xor_2_out, xor_3_out, xor_4_out, xor_5_out, xor_6_out,
       xor_7_out, xor_8_out;

  xor xor_1 (xor_1_out, AddSubControl, B[0]);
  xor xor_2 (xor_2_out, AddSubControl, B[1]);
  xor xor_3 (xor_3_out, AddSubControl, B[2]);
  xor xor_4 (xor_4_out, AddSubControl, B[3]);
  xor xor_5 (xor_5_out, AddSubControl, B[4]);
  xor xor_6 (xor_6_out, AddSubControl, B[5]);
  xor xor_7 (xor_7_out, AddSubControl, B[6]);
  xor xor_8 (xor_8_out, AddSubControl, B[7]);
  not not_1 (not_1_out, xor_8_out);
  fullAdderALU fulladderalu_1 (
    .CarryIn(AddSubControl), .A(A[0]), .B(xor_1_out), .Result(Result[0]), .CarryOut(fulladderalu_1_carryout));
  fullAdderALU fulladderalu_2 (
    .CarryIn(fulladderalu_1_carryout), .A(A[1]), .B(xor_2_out), .Result(Result[1]),
    .CarryOut(fulladderalu_2_carryout));
  fullAdderALU fulladderalu_3 (
    .CarryIn(fulladderalu_2_carryout), .A(A[2]), .B(xor_3_out), .Result(Result[2]),
    .CarryOut(fulladderalu_3_carryout));
  fullAdderALU fulladderalu_4 (
    .CarryIn(fulladderalu_3_carryout), .A(A[3]), .B(xor_4_out), .Result(Result[3]),
    .CarryOut(fulladderalu_4_carryout));
  fullAdderALU fulladderalu_5 (
    .CarryIn(fulladderalu_4_carryout), .A(A[4]), .B(xor_5_out), .Result(Result[4]),
    .CarryOut(fulladderalu_5_carryout));
  fullAdderALU fulladderalu_6 (
    .CarryIn(fulladderalu_5_carryout), .A(A[5]), .B(xor_6_out), .Result(Result[5]),
    .CarryOut(fulladderalu_6_carryout));
  fullAdderALU fulladderalu_7 (
    .CarryIn(fulladderalu_6_carryout), .A(A[6]), .B(xor_7_out), .Result(Result[6]),
    .CarryOut(fulladderalu_7_carryout));
  fullAdderALU fulladderalu_8 (
    .CarryIn(fulladderalu_7_carryout), .A(A[7]), .B(xor_8_out), .Result(Result[7]), .CarryOut(Carry));
  not not_2 (not_2_out, A[7]);
  not not_3 (not_3_out, Result[7]);
  and and_1 (and_1_out, Result[7], not_2_out, not_1_out);
  and and_2 (and_2_out, not_3_out, A[7], A[7]);
  or or_1 (Overflow, and_1_out, and_2_out);
endmodule

module AndALU (
  input  [7:0] A,
  input  [7:0] B,
  output [7:0] Result
);

  and and_1 (Result[0], A[0], B[0]);
  and and_2 (Result[1], A[1], B[1]);
  and and_3 (Result[2], A[2], B[2]);
  and and_4 (Result[3], A[3], B[3]);
  and and_5 (Result[4], A[4], B[4]);
  and and_6 (Result[5], A[5], B[5]);
  and and_7 (Result[6], A[6], B[6]);
  and and_8 (Result[7], A[7], B[7]);
endmodule

module OrALU (
  input  [7:0] A,
  input  [7:0] B,
  output [7:0] Result
);

  or or_1 (Result[0], A[0], B[0]);
  or or_2 (Result[1], A[1], B[1]);
  or or_3 (Result[2], A[2], B[2]);
  or or_4 (Result[3], A[3], B[3]);
  or or_5 (Result[4], A[4], B[4]);
  or or_6 (Result[5], A[5], B[5]);
  or or_7 (Result[6], A[6], B[6]);
  or or_8 (Result[7], A[7], B[7]);
endmodule
