// Logisim project keyboardWbuffer.circ as structural Verilog: 1 circuit, main circuit keyboardwBuffer
module keyboardwBuffer (
  input  b2,
  input  b3,
  input  button2,
  input  b4,
  input  b5,
  input  b6,
  input  b7,
  input  b8,
  input  b9,
  input  reset,
  output [7:0] out_11
);

  wire or_1_out, or_2_out, or_3_out, or_4_out;

  or or_1 (or_1_out, b9, b8);
  or or_2 (or_2_out, b7, b6, b5, b4);
  or or_3 (or_3_out, b7, b6, b3, b2);
  or or_4 (or_4_out, b9, b7, b5, b3, button2);
  S_R_Flip_Flop s_r_ff_1 (.Q(out_11[3]), .reset(reset), .preset(or_1_out));  // open: S, R, clk, Qn
  S_R_Flip_Flop s_r_ff_2 (.Q(out_11[2]), .reset(reset), .preset(or_2_out));  // open: S, R, clk, Qn
  S_R_Flip_Flop s_r_ff_3 (.Q(out_11[1]), .reset(reset), .preset(or_3_out));  // open: S, R, clk, Qn
  S_R_Flip_Flop s_r_ff_4 (.Q(out_11[0]), .reset(reset), .preset(or_4_out));  // open: S, R, clk, Qn
  not not_1 (out_11[7], 1'b1);

  assign out_11[6:4] = {3{out_11[7]}};

  // Notes on the sheet:
  //   Key Pad
  //   Input Buffer-read bottom to top
  //   To System Bus
endmodule
