// Logisim project mainCPU.circ as structural Verilog: 11 circuits, main circuit main
module register8bit (
  input  in_1,
  input  in_2,
  input  in_3,
  input  in_4,
  input  in_5,
  input  in_6,
  input  in_7,
  input  in_8,
  input  in_9,
  input  in_10,
  input  in_11,
  output out_12,
  output out_13,
  output out_14,
  output out_15,
  output out_16,
  output out_17,
  output out_18,
  output out_19
);

  wire and_1_out, and_2_out, and_3_out, and_4_out, and_5_out, and_6_out, and_7_out, and_8_out, and_9_out,
       and_10_out, and_11_out, and_12_out, and_13_out, and_14_out, and_15_out, and_16_out, not_1_out,
       not_2_out, not_3_out, not_4_out, not_5_out, not_6_out, not_7_out, not_8_out, not_9_out, s_r_ff_1_q,
       s_r_ff_2_q, s_r_ff_3_q, s_r_ff_4_q, s_r_ff_5_q, s_r_ff_6_q, s_r_ff_7_q, s_r_ff_8_q;

  and and_1 (and_1_out, in_11, in_8, in_10);
  and and_2 (and_2_out, in_11, not_1_out, in_10);
  not not_1 (not_1_out, in_8);
  and and_3 (and_3_out, in_11, in_7, in_10);
  and and_4 (and_4_out, in_11, not_2_out, in_10);
  not not_2 (not_2_out, in_7);
  and and_5 (and_5_out, in_11, in_6, in_10);
  not not_3 (not_3_out, in_6);
  and and_6 (and_6_out, in_11, not_3_out, in_10);
  and and_7 (and_7_out, in_11, in_5, in_10);
  not not_4 (not_4_out, in_5);
  and and_8 (and_8_out, in_11, not_4_out, in_10);
  and and_9 (and_9_out, in_11, in_4, in_10);
  not not_5 (not_5_out, in_4);
  and and_10 (and_10_out, in_11, not_5_out, in_10);
  and and_11 (and_11_out, in_11, in_3, in_10);
  and and_12 (and_12_out, in_11, not_6_out, in_10);
  not not_6 (not_6_out, in_3);
  and and_13 (and_13_out, in_11, in_2, in_10);
  not not_7 (not_7_out, in_2);
  and and_14 (and_14_out, in_11, not_7_out, in_10);
  and and_15 (and_15_out, in_11, in_1, in_10);
  not not_8 (not_8_out, in_1);
  and and_16 (and_16_out, in_11, not_8_out, in_10);
  S_R_Flip_Flop s_r_ff_1 (.S(and_1_out), .R(and_2_out), .clk(in_9), .Q(s_r_ff_1_q));  // open: reset, Qn, preset
  S_R_Flip_Flop s_r_ff_2 (.S(and_3_out), .R(and_4_out), .clk(in_9), .Q(s_r_ff_2_q));  // open: reset, Qn, preset
  S_R_Flip_Flop s_r_ff_3 (.S(and_5_out), .R(and_6_out), .clk(in_9), .Q(s_r_ff_3_q));  // open: reset, Qn, preset
  S_R_Flip_Flop s_r_ff_4 (.S(and_7_out), .R(and_8_out), .clk(in_9), .Q(s_r_ff_4_q));  // open: reset, Qn, preset
  S_R_Flip_Flop s_r_ff_5 (.S(and_9_out), .R(and_10_out), .clk(in_9), .Q(s_r_ff_5_q));  // open: reset, Qn, preset
  S_R_Flip_Flop s_r_ff_6 (.S(and_11_out), .R(and_12_out), .clk(in_9), .Q(s_r_ff_6_q));  // open: reset, Qn, preset
  S_R_Flip_Flop s_r_ff_7 (.S(and_13_out), .R(and_14_out), .clk(in_9), .Q(s_r_ff_7_q));  // open: reset, Qn, preset
  S_R_Flip_Flop s_r_ff_8 (.S(and_15_out), .R(and_16_out), .clk(in_9), .Q(s_r_ff_8_q));  // open: reset, Qn, preset
  not not_9 (not_9_out, in_10);
  and and_17 (out_12, s_r_ff_1_q, not_9_out, in_11);
  and and_18 (out_13, s_r_ff_2_q, not_9_out, in_11);
  and and_19 (out_14, s_r_ff_3_q, not_9_out, in_11);
  and and_20 (out_15, s_r_ff_4_q, not_9_out, in_11);
  and and_21 (out_16, s_r_ff_5_q, not_9_out, in_11);
  and and_22 (out_17, s_r_ff_6_q, not_9_out, in_11);
  and and_23 (out_18, s_r_ff_7_q, not_9_out, in_11);
  and and_24 (out_19, s_r_ff_8_q, not_9_out, in_11);
endmodule

module ram16byte (
  input  [7:0] in_1,
  input  in_2,
  input  in_3,
  input  [3:0] in_4,
  output [7:0] out_5
);

  wire decoder_1_out0, decoder_1_out1, decoder_1_out2, decoder_1_out3, decoder_1_out4, decoder_1_out5,
       decoder_1_out6, decoder_1_out7, decoder_1_out8, decoder_1_out9, decoder_1_out10, decoder_1_out11,
       decoder_1_out12, decoder_1_out13, decoder_1_out14, decoder_1_out15, or_1_out, or_2_out, or_3_out,
       or_4_out, or_5_out, or_6_out, or_7_out, or_8_out, or_9_out, or_10_out, or_11_out, or_12_out,
       or_13_out, or_14_out, or_15_out, or_16_out, or_17_out, or_18_out, or_19_out, or_20_out, or_21_out,
       or_22_out, or_23_out, or_24_out, or_25_out, or_26_out, or_27_out, or_28_out, or_29_out, or_30_out,
       or_31_out, or_32_out, or_33_out, or_34_out, or_35_out, or_36_out, or_37_out, or_38_out, or_39_out,
       or_40_out, or_41_out, or_42_out, or_43_out, or_44_out, or_45_out, or_46_out, or_47_out, or_48_out,
       or_49_out, or_50_out, or_51_out, or_52_out, or_53_out, or_54_out, or_55_out, or_56_out, or_57_out,
       or_58_out, or_59_out, or_60_out, or_61_out, or_62_out, or_63_out, or_64_out, or_65_out, or_66_out,
       or_67_out, or_68_out, or_69_out, or_70_out, or_71_out, or_72_out, or_73_out, or_74_out, or_75_out,
       or_76_out, or_77_out, or_78_out, or_79_out, or_80_out, or_81_out, or_82_out, or_83_out, or_84_out,
       or_85_out, or_86_out, or_87_out, or_88_out, or_89_out, or_90_out, or_91_out, or_92_out, or_93_out,
       or_94_out, or_95_out, or_96_out, or_97_out, or_98_out, or_99_out, or_100_out, or_101_out, or_102_out,
       or_103_out, or_104_out, or_105_out, or_106_out, or_107_out, or_108_out, or_109_out, or_110_out,
       or_111_out, or_112_out;
  wire [7:0] register8bit_1_out_12, register8bit_2_out_12, register8bit_3_out_12, register8bit_4_out_12,
       register8bit_5_out_12, register8bit_6_out_12, register8bit_7_out_12, register8bit_8_out_12,
       register8bit_9_out_12, register8bit_10_out_12, register8bit_11_out_12, register8bit_12_out_12,
       register8bit_13_out_12, register8bit_14_out_12, register8bit_15_out_12, register8bit_16_out_12;

  Decoder #(.select(4)) decoder_1 (
    .out0(decoder_1_out0), .out1(decoder_1_out1), .out2(decoder_1_out2), .out3(decoder_1_out3),
    .out4(decoder_1_out4), .out5(decoder_1_out5), .out6(decoder_1_out6), .out7(decoder_1_out7),
    .out8(decoder_1_out8), .out9(decoder_1_out9), .out10(decoder_1_out10), .out11(decoder_1_out11),
    .out12(decoder_1_out12), .out13(decoder_1_out13), .out14(decoder_1_out14), .out15(decoder_1_out15),
    .sel(in_4));  // open: en
  or or_1 (or_1_out, register8bit_2_out_12[0], register8bit_1_out_12[0]);
  or or_2 (or_2_out, register8bit_2_out_12[1], register8bit_1_out_12[1]);
  or or_3 (or_3_out, register8bit_2_out_12[2], register8bit_1_out_12[2]);
  or or_4 (or_4_out, register8bit_2_out_12[3], register8bit_1_out_12[3]);
  or or_5 (or_5_out, register8bit_2_out_12[4], register8bit_1_out_12[4]);
  or or_6 (or_6_out, register8bit_2_out_12[5], register8bit_1_out_12[5]);
  or or_7 (or_7_out, register8bit_2_out_12[6], register8bit_1_out_12[6]);
  or or_8 (or_8_out, register8bit_2_out_12[7], register8bit_1_out_12[7]);
  register8bit register8bit_1 (
    .in_10(in_2), .in_8(in_1[0]), .in_7(in_1[1]), .in_6(in_1[2]), .in_5(in_1[3]), .in_4(in_1[4]),
    .in_3(in_1[5]), .in_2(in_1[6]), .in_1(in_1[7]), .in_11(decoder_1_out3),
    .out_12(register8bit_1_out_12[0]), .out_13(register8bit_1_out_12[1]), .out_14(register8bit_1_out_12[2]),
    .out_15(register8bit_1_out_12[3]), .out_16(register8bit_1_out_12[4]), .out_17(register8bit_1_out_12[5]),
    .out_18(register8bit_1_out_12[6]), .out_19(register8bit_1_out_12[7]), .in_9(in_3));
  register8bit register8bit_2 (
    .in_10(in_2), .in_8(in_1[0]), .in_7(in_1[1]), .in_6(in_1[2]), .in_5(in_1[3]), .in_4(in_1[4]),
    .in_3(in_1[5]), .in_2(in_1[6]), .in_1(in_1[7]), .in_11(decoder_1_out7),
    .out_12(register8bit_2_out_12[0]), .out_13(register8bit_2_out_12[1]), .out_14(register8bit_2_out_12[2]),
    .out_15(register8bit_2_out_12[3]), .out_16(register8bit_2_out_12[4]), .out_17(register8bit_2_out_12[5]),
    .out_18(register8bit_2_out_12[6]), .out_19(register8bit_2_out_12[7]), .in_9(in_3));
  register8bit register8bit_3 (
    .in_10(in_2), .in_8(in_1[0]), .in_7(in_1[1]), .in_6(in_1[2]), .in_5(in_1[3]), .in_4(in_1[4]),
    .in_3(in_1[5]), .in_2(in_1[6]), .in_1(in_1[7]), .in_11(decoder_1_out11),
    .out_12(register8bit_3_out_12[0]), .out_13(register8bit_3_out_12[1]), .out_14(register8bit_3_out_12[2]),
    .out_15(register8bit_3_out_12[3]), .out_16(register8bit_3_out_12[4]), .out_17(register8bit_3_out_12[5]),
    .out_18(register8bit_3_out_12[6]), .out_19(register8bit_3_out_12[7]), .in_9(in_3));
  register8bit register8bit_4 (
    .in_10(in_2), .in_8(in_1[0]), .in_7(in_1[1]), .in_6(in_1[2]), .in_5(in_1[3]), .in_4(in_1[4]),
    .in_3(in_1[5]), .in_2(in_1[6]), .in_1(in_1[7]), .in_11(decoder_1_out15),
    .out_12(register8bit_4_out_12[0]), .out_13(register8bit_4_out_12[1]), .out_14(register8bit_4_out_12[2]),
    .out_15(register8bit_4_out_12[3]), .out_16(register8bit_4_out_12[4]), .out_17(register8bit_4_out_12[5]),
    .out_18(register8bit_4_out_12[6]), .out_19(register8bit_4_out_12[7]), .in_9(in_3));
  or or_9 (or_9_out, register8bit_3_out_12[0], or_1_out);
  or or_10 (or_10_out, register8bit_3_out_12[1], or_2_out);
  or or_11 (or_11_out, register8bit_3_out_12[2], or_3_out);
  or or_12 (or_12_out, register8bit_3_out_12[3], or_4_out);
  or or_13 (or_13_out, register8bit_3_out_12[4], or_5_out);
  or or_14 (or_14_out, register8bit_3_out_12[5], or_6_out);
  or or_15 (or_15_out, register8bit_3_out_12[6], or_7_out);
  or or_16 (or_16_out, register8bit_3_out_12[7], or_8_out);
  or or_17 (or_17_out, register8bit_4_out_12[0], or_9_out);
  or or_18 (or_18_out, register8bit_4_out_12[1], or_10_out);
  or or_19 (or_19_out, register8bit_4_out_12[2], or_11_out);
  or or_20 (or_20_out, register8bit_4_out_12[3], or_12_out);
  or or_21 (or_21_out, register8bit_4_out_12[4], or_13_out);
  or or_22 (or_22_out, register8bit_4_out_12[5], or_14_out);
  or or_23 (or_23_out, register8bit_4_out_12[6], or_15_out);
  or or_24 (or_24_out, register8bit_4_out_12[7], or_16_out);
  register8bit register8bit_5 (
    .in_10(in_2), .in_8(in_1[0]), .in_7(in_1[1]), .in_6(in_1[2]), .in_5(in_1[3]), .in_4(in_1[4]),
    .in_3(in_1[5]), .in_2(in_1[6]), .in_1(in_1[7]), .in_11(decoder_1_out2),
    .out_12(register8bit_5_out_12[0]), .out_13(register8bit_5_out_12[1]), .out_14(register8bit_5_out_12[2]),
    .out_15(register8bit_5_out_12[3]), .out_16(register8bit_5_out_12[4]), .out_17(register8bit_5_out_12[5]),
    .out_18(register8bit_5_out_12[6]), .out_19(register8bit_5_out_12[7]), .in_9(in_3));
  register8bit register8bit_6 (
    .in_10(in_2), .in_8(in_1[0]), .in_7(in_1[1]), .in_6(in_1[2]), .in_5(in_1[3]), .in_4(in_1[4]),
    .in_3(in_1[5]), .in_2(in_1[6]), .in_1(in_1[7]), .in_11(decoder_1_out6),
    .out_12(register8bit_6_out_12[0]), .out_13(register8bit_6_out_12[1]), .out_14(register8bit_6_out_12[2]),
    .out_15(register8bit_6_out_12[3]), .out_16(register8bit_6_out_12[4]), .out_17(register8bit_6_out_12[5]),
    .out_18(register8bit_6_out_12[6]), .out_19(register8bit_6_out_12[7]), .in_9(in_3));
  register8bit register8bit_7 (
    .in_10(in_2), .in_8(in_1[0]), .in_7(in_1[1]), .in_6(in_1[2]), .in_5(in_1[3]), .in_4(in_1[4]),
    .in_3(in_1[5]), .in_2(in_1[6]), .in_1(in_1[7]), .in_11(decoder_1_out10),
    .out_12(register8bit_7_out_12[0]), .out_13(register8bit_7_out_12[1]), .out_14(register8bit_7_out_12[2]),
    .out_15(register8bit_7_out_12[3]), .out_16(register8bit_7_out_12[4]), .out_17(register8bit_7_out_12[5]),
    .out_18(register8bit_7_out_12[6]), .out_19(register8bit_7_out_12[7]), .in_9(in_3));
  register8bit register8bit_8 (
    .in_10(in_2), .in_8(in_1[0]), .in_7(in_1[1]), .in_6(in_1[2]), .in_5(in_1[3]), .in_4(in_1[4]),
    .in_3(in_1[5]), .in_2(in_1[6]), .in_1(in_1[7]), .in_11(decoder_1_out14),
    .out_12(register8bit_8_out_12[0]), .out_13(register8bit_8_out_12[1]), .out_14(register8bit_8_out_12[2]),
    .out_15(register8bit_8_out_12[3]), .out_16(register8bit_8_out_12[4]), .out_17(register8bit_8_out_12[5]),
    .out_18(register8bit_8_out_12[6]), .out_19(register8bit_8_out_12[7]), .in_9(in_3));
  or or_25 (or_25_out, register8bit_6_out_12[0], or_17_out);
  or or_26 (or_26_out, register8bit_6_out_12[1], or_18_out);
  or or_27 (or_27_out, register8bit_6_out_12[2], or_19_out);
  or or_28 (or_28_out, register8bit_6_out_12[3], or_20_out);
  or or_29 (or_29_out, register8bit_6_out_12[4], or_21_out);
  or or_30 (or_30_out, register8bit_6_out_12[5], or_22_out);
  or or_31 (or_31_out, register8bit_6_out_12[6], or_23_out);
  or or_32 (or_32_out, register8bit_6_out_12[7], or_24_out);
  or or_33 (or_33_out, register8bit_5_out_12[0], or_25_out);
  or or_34 (or_34_out, register8bit_5_out_12[1], or_26_out);
  or or_35 (or_35_out, register8bit_5_out_12[2], or_27_out);
  or or_36 (or_36_out, register8bit_5_out_12[3], or_28_out);
  or or_37 (or_37_out, register8bit_5_out_12[4], or_29_out);
  or or_38 (or_38_out, register8bit_5_out_12[5], or_30_out);
  or or_39 (or_39_out, register8bit_5_out_12[6], or_31_out);
  or or_40 (or_40_out, register8bit_5_out_12[7], or_32_out);
  or or_41 (or_41_out, register8bit_7_out_12[0], or_33_out);
  or or_42 (or_42_out, register8bit_7_out_12[1], or_34_out);
  or or_43 (or_43_out, register8bit_7_out_12[2], or_35_out);
  or or_44 (or_44_out, register8bit_7_out_12[3], or_36_out);
  or or_45 (or_45_out, register8bit_7_out_12[4], or_37_out);
  or or_46 (or_46_out, register8bit_7_out_12[5], or_38_out);
  or or_47 (or_47_out, register8bit_7_out_12[6], or_39_out);
  or or_48 (or_48_out, register8bit_7_out_12[7], or_40_out);
  register8bit register8bit_9 (
    .in_10(in_2), .in_8(in_1[0]), .in_7(in_1[1]), .in_6(in_1[2]), .in_5(in_1[3]), .in_4(in_1[4]),
    .in_3(in_1[5]), .in_2(in_1[6]), .in_1(in_1[7]), .in_11(decoder_1_out1),
    .out_12(register8bit_9_out_12[0]), .out_13(register8bit_9_out_12[1]), .out_14(register8bit_9_out_12[2]),
    .out_15(register8bit_9_out_12[3]), .out_16(register8bit_9_out_12[4]), .out_17(register8bit_9_out_12[5]),
    .out_18(register8bit_9_out_12[6]), .out_19(register8bit_9_out_12[7]), .in_9(in_3));
  register8bit register8bit_10 (
    .in_10(in_2), .in_8(in_1[0]), .in_7(in_1[1]), .in_6(in_1[2]), .in_5(in_1[3]), .in_4(in_1[4]),
    .in_3(in_1[5]), .in_2(in_1[6]), .in_1(in_1[7]), .in_11(decoder_1_out5),
    .out_12(register8bit_10_out_12[0]), .out_13(register8bit_10_out_12[1]),
    .out_14(register8bit_10_out_12[2]), .out_15(register8bit_10_out_12[3]),
    .out_16(register8bit_10_out_12[4]), .out_17(register8bit_10_out_12[5]),
    .out_18(register8bit_10_out_12[6]), .out_19(register8bit_10_out_12[7]), .in_9(in_3));
  register8bit register8bit_11 (
    .in_10(in_2), .in_8(in_1[0]), .in_7(in_1[1]), .in_6(in_1[2]), .in_5(in_1[3]), .in_4(in_1[4]),
    .in_3(in_1[5]), .in_2(in_1[6]), .in_1(in_1[7]), .in_11(decoder_1_out9),
    .out_12(register8bit_11_out_12[0]), .out_13(register8bit_11_out_12[1]),
    .out_14(register8bit_11_out_12[2]), .out_15(register8bit_11_out_12[3]),
    .out_16(register8bit_11_out_12[4]), .out_17(register8bit_11_out_12[5]),
    .out_18(register8bit_11_out_12[6]), .out_19(register8bit_11_out_12[7]), .in_9(in_3));
  register8bit register8bit_12 (
    .in_10(in_2), .in_8(in_1[0]), .in_7(in_1[1]), .in_6(in_1[2]), .in_5(in_1[3]), .in_4(in_1[4]),
    .in_3(in_1[5]), .in_2(in_1[6]), .in_1(in_1[7]), .in_11(decoder_1_out13),
    .out_12(register8bit_12_out_12[0]), .out_13(register8bit_12_out_12[1]),
    .out_14(register8bit_12_out_12[2]), .out_15(register8bit_12_out_12[3]),
    .out_16(register8bit_12_out_12[4]), .out_17(register8bit_12_out_12[5]),
    .out_18(register8bit_12_out_12[6]), .out_19(register8bit_12_out_12[7]), .in_9(in_3));
  or or_49 (or_49_out, register8bit_8_out_12[0], or_41_out);
  or or_50 (or_50_out, register8bit_8_out_12[1], or_42_out);
  or or_51 (or_51_out, register8bit_8_out_12[2], or_43_out);
  or or_52 (or_52_out, register8bit_8_out_12[3], or_44_out);
  or or_53 (or_53_out, register8bit_8_out_12[4], or_45_out);
  or or_54 (or_54_out, register8bit_8_out_12[5], or_46_out);
  or or_55 (or_55_out, register8bit_8_out_12[6], or_47_out);
  or or_56 (or_56_out, register8bit_8_out_12[7], or_48_out);
  or or_57 (or_57_out, register8bit_12_out_12[0], or_49_out);
  or or_58 (or_58_out, register8bit_12_out_12[1], or_50_out);
  or or_59 (or_59_out, register8bit_12_out_12[2], or_51_out);
  or or_60 (or_60_out, register8bit_12_out_12[3], or_52_out);
  or or_61 (or_61_out, register8bit_12_out_12[4], or_53_out);
  or or_62 (or_62_out, register8bit_12_out_12[5], or_54_out);
  or or_63 (or_63_out, register8bit_12_out_12[6], or_55_out);
  or or_64 (or_64_out, register8bit_12_out_12[7], or_56_out);
  or or_65 (or_65_out, register8bit_11_out_12[0], or_57_out);
  or or_66 (or_66_out, register8bit_11_out_12[1], or_58_out);
  or or_67 (or_67_out, register8bit_11_out_12[2], or_59_out);
  or or_68 (or_68_out, register8bit_11_out_12[3], or_60_out);
  or or_69 (or_69_out, register8bit_11_out_12[4], or_61_out);
  or or_70 (or_70_out, register8bit_11_out_12[5], or_62_out);
  or or_71 (or_71_out, register8bit_11_out_12[6], or_63_out);
  or or_72 (or_72_out, register8bit_11_out_12[7], or_64_out);
  register8bit register8bit_13 (
    .in_10(in_2), .in_8(in_1[0]), .in_7(in_1[1]), .in_6(in_1[2]), .in_5(in_1[3]), .in_4(in_1[4]),
    .in_3(in_1[5]), .in_2(in_1[6]), .in_1(in_1[7]), .in_11(decoder_1_out0),
    .out_12(register8bit_13_out_12[0]), .out_13(register8bit_13_out_12[1]),
    .out_14(register8bit_13_out_12[2]), .out_15(register8bit_13_out_12[3]),
    .out_16(register8bit_13_out_12[4]), .out_17(register8bit_13_out_12[5]),
    .out_18(register8bit_13_out_12[6]), .out_19(register8bit_13_out_12[7]), .in_9(in_3));
  register8bit register8bit_14 (
    .in_10(in_2), .in_8(in_1[0]), .in_7(in_1[1]), .in_6(in_1[2]), .in_5(in_1[3]), .in_4(in_1[4]),
    .in_3(in_1[5]), .in_2(in_1[6]), .in_1(in_1[7]), .in_11(decoder_1_out4),
    .out_12(register8bit_14_out_12[0]), .out_13(register8bit_14_out_12[1]),
    .out_14(register8bit_14_out_12[2]), .out_15(register8bit_14_out_12[3]),
    .out_16(register8bit_14_out_12[4]), .out_17(register8bit_14_out_12[5]),
    .out_18(register8bit_14_out_12[6]), .out_19(register8bit_14_out_12[7]), .in_9(in_3));
  register8bit register8bit_15 (
    .in_10(in_2), .in_8(in_1[0]), .in_7(in_1[1]), .in_6(in_1[2]), .in_5(in_1[3]), .in_4(in_1[4]),
    .in_3(in_1[5]), .in_2(in_1[6]), .in_1(in_1[7]), .in_11(decoder_1_out8),
    .out_12(register8bit_15_out_12[0]), .out_13(register8bit_15_out_12[1]),
    .out_14(register8bit_15_out_12[2]), .out_15(register8bit_15_out_12[3]),
    .out_16(register8bit_15_out_12[4]), .out_17(register8bit_15_out_12[5]),
    .out_18(register8bit_15_out_12[6]), .out_19(register8bit_15_out_12[7]), .in_9(in_3));
  register8bit register8bit_16 (
    .in_10(in_2), .in_8(in_1[0]), .in_7(in_1[1]), .in_6(in_1[2]), .in_5(in_1[3]), .in_4(in_1[4]),
    .in_3(in_1[5]), .in_2(in_1[6]), .in_1(in_1[7]), .in_11(decoder_1_out12),
    .out_12(register8bit_16_out_12[0]), .out_13(register8bit_16_out_12[1]),
    .out_14(register8bit_16_out_12[2]), .out_15(register8bit_16_out_12[3]),
    .out_16(register8bit_16_out_12[4]), .out_17(register8bit_16_out_12[5]),
    .out_18(register8bit_16_out_12[6]), .out_19(register8bit_16_out_12[7]), .in_9(in_3));
  or or_73 (or_73_out, register8bit_10_out_12[0], or_65_out);
  or or_74 (or_74_out, register8bit_10_out_12[1], or_66_out);
  or or_75 (or_75_out, register8bit_10_out_12[2], or_67_out);
  or or_76 (or_76_out, register8bit_10_out_12[3], or_68_out);
  or or_77 (or_77_out, register8bit_10_out_12[4], or_69_out);
  or or_78 (or_78_out, register8bit_10_out_12[5], or_70_out);
  or or_79 (or_79_out, register8bit_10_out_12[6], or_71_out);
  or or_80 (or_80_out, register8bit_10_out_12[7], or_72_out);
  or or_81 (or_81_out, register8bit_9_out_12[0], or_73_out);
  or or_82 (or_82_out, register8bit_9_out_12[1], or_74_out);
  or or_83 (or_83_out, register8bit_9_out_12[2], or_75_out);
  or or_84 (or_84_out, register8bit_9_out_12[3], or_76_out);
  or or_85 (or_85_out, register8bit_9_out_12[4], or_77_out);
  or or_86 (or_86_out, register8bit_9_out_12[5], or_78_out);
  or or_87 (or_87_out, register8bit_9_out_12[6], or_79_out);
  or or_88 (or_88_out, register8bit_9_out_12[7], or_80_out);
  or or_89 (or_89_out, register8bit_13_out_12[0], or_81_out);
  or or_90 (or_90_out, register8bit_13_out_12[1], or_82_out);
  or or_91 (or_91_out, register8bit_13_out_12[2], or_83_out);
  or or_92 (or_92_out, register8bit_13_out_12[3], or_84_out);
  or or_93 (or_93_out, register8bit_13_out_12[4], or_85_out);
  or or_94 (or_94_out, register8bit_13_out_12[5], or_86_out);
  or or_95 (or_95_out, register8bit_13_out_12[6], or_87_out);
  or or_96 (or_96_out, register8bit_13_out_12[7], or_88_out);
  or or_97 (or_97_out, register8bit_14_out_12[0], or_89_out);
  or or_98 (or_98_out, register8bit_14_out_12[1], or_90_out);
  or or_99 (or_99_out, register8bit_14_out_12[2], or_91_out);
  or or_100 (or_100_out, register8bit_14_out_12[3], or_92_out);
  or or_101 (or_101_out, register8bit_14_out_12[4], or_93_out);
  or or_102 (or_102_out, register8bit_14_out_12[5], or_94_out);
  or or_103 (or_103_out, register8bit_14_out_12[6], or_95_out);
  or or_104 (or_104_out, register8bit_14_out_12[7], or_96_out);
  or or_105 (or_105_out, register8bit_15_out_12[0], or_97_out);
  or or_106 (or_106_out, register8bit_15_out_12[1], or_98_out);
  or or_107 (or_107_out, register8bit_15_out_12[2], or_99_out);
  or or_108 (or_108_out, register8bit_15_out_12[3], or_100_out);
  or or_109 (or_109_out, register8bit_15_out_12[4], or_101_out);
  or or_110 (or_110_out, register8bit_15_out_12[5], or_102_out);
  or or_111 (or_111_out, register8bit_15_out_12[6], or_103_out);
  or or_112 (or_112_out, register8bit_15_out_12[7], or_104_out);
  or or_113 (out_5[0], register8bit_16_out_12[0], or_105_out);
  or or_114 (out_5[1], register8bit_16_out_12[1], or_106_out);
  or or_115 (out_5[2], register8bit_16_out_12[2], or_107_out);
  or or_116 (out_5[3], register8bit_16_out_12[3], or_108_out);
  or or_117 (out_5[4], register8bit_16_out_12[4], or_109_out);
  or or_118 (out_5[5], register8bit_16_out_12[5], or_110_out);
  or or_119 (out_5[6], register8bit_16_out_12[6], or_111_out);
  or or_120 (out_5[7], register8bit_16_out_12[7], or_112_out);

  // Other names for the same wires on the sheet: clock = in_3; rwbit = in_2
endmodule

module jkcounter4bit (
  input  clk,
  input  reset,
  output [3:0] countoutput
);

  wire and_1_out, and_2_out;

  J_K_Flip_Flop j_k_ff_1 (.J(1'b1), .K(1'b1), .clk(clk), .Q(countoutput[0]), .reset(reset));  // open: Qn, preset
  J_K_Flip_Flop j_k_ff_2 (
    .J(countoutput[0]), .K(countoutput[0]), .clk(clk), .Q(countoutput[1]), .reset(reset));  // open: Qn, preset
  and and_1 (and_1_out, countoutput[0], countoutput[1]);
  J_K_Flip_Flop j_k_ff_3 (
    .J(and_1_out), .K(and_1_out), .clk(clk), .Q(countoutput[2]), .reset(reset));  // open: Qn, preset
  J_K_Flip_Flop j_k_ff_4 (
    .J(and_2_out), .K(and_2_out), .clk(clk), .Q(countoutput[3]), .reset(reset));  // open: Qn, preset
  and and_2 (and_2_out, and_1_out, countoutput[2]);
endmodule

module dRegister (
  input  in_1,
  input  [7:0] in_2,
  output [7:0] out_3
);

  D_Flip_Flop d_ff_1 (.D(in_2[0]), .clk(in_1), .Q(out_3[0]));  // open: Qn, preset, reset
  D_Flip_Flop d_ff_2 (.D(in_2[1]), .clk(in_1), .Q(out_3[1]));  // open: Qn, preset, reset
  D_Flip_Flop d_ff_3 (.D(in_2[2]), .clk(in_1), .Q(out_3[2]));  // open: Qn, preset, reset
  D_Flip_Flop d_ff_4 (.D(in_2[3]), .clk(in_1), .Q(out_3[3]));  // open: Qn, preset, reset
  D_Flip_Flop d_ff_5 (.D(in_2[4]), .clk(in_1), .Q(out_3[4]));  // open: Qn, preset, reset
  D_Flip_Flop d_ff_6 (.D(in_2[5]), .clk(in_1), .Q(out_3[5]));  // open: Qn, preset, reset
  D_Flip_Flop d_ff_7 (.D(in_2[6]), .clk(in_1), .Q(out_3[6]));  // open: Qn, preset, reset
  D_Flip_Flop d_ff_8 (.D(in_2[7]), .clk(in_1), .Q(out_3[7]));  // open: Qn, preset, reset
endmodule

module main (
  input  in_1,
  input  in_2,
  input  in_3,
  input  in_4,
  input  in_5,
  input  in_6,
  input  in_7,
  input  in_8,
  input  in_9,
  input  in_10,
  input  in_11,
  input  in_12,
  input  in_13,
  input  in_14,
  input  in_15,
  input  in_16,
  input  in_17,
  input  in_18,
  input  in_19,
  input  in_20,
  input  in_21,
  input  in_22,
  input  in_23,
  input  in_24,
  input  in_25
);

  wire ADDSUB, ALUandOr, ALUmathlogic, ALUtoCPUBUS, and_1_out, and_2_out, and_3_out, and_4_out, and_5_out,
       and_6_out, and_7_out, and_8_out, and_9_out, and_10_out, and_11_out, and_12_out, and_13_out,
       and_14_out, and_15_out, and_16_out, and_17_out, and_18_out, and_19_out, and_20_out, and_21_out,
       and_22_out, and_23_out, and_24_out, and_25_out, and_26_out, and_27_out, and_28_out, and_29_out,
       and_30_out, and_32_out, and_35_out, and_36_out, and_37_out, and_38_out, and_39_out, and_40_out,
       and_41_out, and_42_out, and_43_out, and_44_out, and_45_out, and_46_out, and_47_out, and_48_out,
       and_49_out, and_50_out, and_51_out, and_52_out, ARtoRAM, b1_out, b2_out, b3_out, b4_out, b5_out,
       b6_out, b7_out, b8_out, b9_out, branch, BUStoAR, BUStoMBR, BUStoPRINT, clk, CPUBUStoALUL,
       CPUBUStoALUR, CPUBUStoMBR, CPUBUStoR1, CPUBUStoR2, decoder_1_out0, decoder_1_out1, decoder_1_out2,
       decoder_1_out3, decoder_1_out4, decoder_1_out5, decoder_1_out13, DRINPUT, DRtoBUS,
       equivalence_1_out_3, INPtoBUS, mainalu_1_overflow, MARtoBUS, MARtoCPUBUS, MBRtoBUS, MBRtoCPUBUS,
       MBRtoIR, nand_1_out, not_2_out, not_3_out, not_4_out, not_5_out, not_6_out, not_7_out, not_8_out,
       not_9_out, not_10_out, not_11_out, not_12_out, not_13_out, not_14_out, not_15_out, not_16_out,
       not_17_out, not_18_out, not_19_out, not_20_out, not_21_out, not_22_out, not_23_out, not_24_out,
       not_25_out, not_26_out, not_27_out, not_28_out, not_29_out, not_30_out, not_31_out, not_32_out,
       not_33_out, not_34_out, not_35_out, or_2_out, or_3_out, or_5_out, or_6_out, or_7_out, or_8_out,
       or_9_out, or_10_out, or_11_out, or_12_out, or_14_out, or_15_out, PCplus1, PCtoMAR, R1toCPUBUS,
       R2toCPUBUS, RAMtoDR, romdump_1_out_3, ROMtoRAM, RWBIT, zeroreset_out;
  wire [3:0] jkcounter4bit_1_countoutput, Rom_out_2, ROMINPUT, undriven_4;
  wire [6:0] decoder_1_out12;
  wire [7:0] add1_1_out_2, AR_out_3, branchadd, DR_out_3, dregister_1_out_3, gate_1_out_3, gate_2_out_3,
       gate_3_out_3, gate_4_out_3, gate_5_out_3, gate_6_out_3, gate_7_out_3, gate_8_out_3, gate_9_out_3,
       gate_10_out_3, gate_11_out_3, gate_12_out_3, gate_14_out_3, gate_15_out_3, gate_16_out_3,
       gate_17_out_3, gate_18_out_3, gate_19_out_3, gate_20_out_3, gate_21_out_3, gate_22_out_3,
       gate_23_out_3, gate_24_out_3, gate_25_out_3, gate_26_out_3, gate_27_out_3, gate_28_out_3, IR_out_3,
       keyboardwbuffer_1_out_11, L_out_3, mainalu_1_result, MAR_out_3, MBR_out_3, multiplexer_1_out,
       or_1_out, or_4_out, or_13_out, or_20_out, or_21_out, or_28_out, or_29_out, PC_out_3, R_out_3,
       ram16byte_1_out_5, Rom_out_3;
  wire [7:4] undriven, undriven_2, undriven_3;
  wire [15:0] R1_out_3;

  dRegister PC (.in_2(multiplexer_1_out), .out_3(PC_out_3), .in_1(PCplus1));
  Multiplexer #(.width(8), .enable("false")) multiplexer_1 (
    .in0(add1_1_out_2), .in1(branchadd), .out(multiplexer_1_out), .sel(branch));
  Clock clock_1 (.out(clk));
  // Probe on PC_out_3
  add1 add1_1 (.out_2(add1_1_out_2), .in_1(PC_out_3));
  and and_1 (and_1_out, clk, and_16_out, romdump_1_out_3);
  ROMDump romdump_1 (.in_1(clk), .out_2(ROMINPUT), .out_3(romdump_1_out_3));
  not not_1 (ROMtoRAM, romdump_1_out_3);
  not not_2 (not_2_out, IR_out_3[0]);
  not not_3 (not_3_out, IR_out_3[1]);
  not not_4 (not_4_out, IR_out_3[2]);
  not not_5 (not_5_out, IR_out_3[3]);
  not not_6 (not_6_out, IR_out_3[4]);
  not not_7 (not_7_out, IR_out_3[5]);
  not not_8 (not_8_out, IR_out_3[6]);
  not not_9 (not_9_out, IR_out_3[7]);
  assign or_1_out = gate_8_out_3 | gate_7_out_3;  // OR_Gate or_1, 8 bits wide
  gate gate_1 (.in_2(PCtoMAR), .in_1(PC_out_3), .out_3(gate_1_out_3));
  gate gate_2 (.in_2(BUStoMBR), .in_1(or_20_out), .out_3(gate_2_out_3));
  gate gate_3 (.in_2(CPUBUStoMBR), .in_1(or_13_out), .out_3(gate_3_out_3));
  gate gate_4 (.in_2(CPUBUStoR1), .in_1(or_13_out), .out_3(gate_4_out_3));
  gate gate_5 (.in_2(CPUBUStoR2), .in_1(or_13_out), .out_3(gate_5_out_3));
  gate gate_6 (.in_2(MBRtoIR), .in_1(MBR_out_3), .out_3(gate_6_out_3));
  jkcounter4bit jkcounter4bit_1 (.clk(and_1_out), .reset(decoder_1_out13), .countoutput(jkcounter4bit_1_countoutput));
  nand nand_1 (nand_1_out, not_2_out, not_3_out, not_4_out, not_5_out, decoder_1_out12[6], not_6_out, not_7_out, not_8_out, not_9_out);
  not not_10 (not_10_out, IR_out_3[6]);
  not not_11 (not_11_out, IR_out_3[5]);
  not not_12 (not_12_out, IR_out_3[6]);
  not not_13 (not_13_out, IR_out_3[7]);
  not not_14 (not_14_out, IR_out_3[6]);
  not not_15 (not_15_out, IR_out_3[5]);
  not not_16 (not_16_out, IR_out_3[7]);
  not not_17 (not_17_out, IR_out_3[6]);
  not not_18 (not_18_out, IR_out_3[4]);
  or or_2 (or_2_out, decoder_1_out12[2], decoder_1_out12[1]);
  not not_19 (not_19_out, IR_out_3[7]);
  not not_20 (not_20_out, IR_out_3[6]);
  not not_21 (not_21_out, IR_out_3[5]);
  not not_22 (not_22_out, IR_out_3[4]);
  not not_23 (not_23_out, IR_out_3[7]);
  not not_24 (not_24_out, IR_out_3[6]);
  dRegister MAR (.in_2(gate_1_out_3), .out_3(MAR_out_3), .in_1(and_9_out));
  or or_3 (or_3_out, CPUBUStoMBR, BUStoMBR);
  dRegister MBR (.in_2(or_4_out), .out_3(MBR_out_3), .in_1(and_10_out));
  assign or_4_out = gate_2_out_3 | gate_3_out_3;  // OR_Gate or_4, 8 bits wide
  dRegister R1 (.in_2(gate_4_out_3), .out_3(R1_out_3[7:0]), .in_1(and_11_out));
  dRegister R2 (.in_2(gate_5_out_3), .out_3(R1_out_3[15:8]), .in_1(and_12_out));
  dRegister IR (.in_2(gate_6_out_3), .out_3(IR_out_3), .in_1(and_13_out));
  and and_2 (and_2_out, IR_out_3[7], not_10_out, not_11_out);
  and and_3 (and_3_out, IR_out_3[7], not_12_out, IR_out_3[5]);
  and and_4 (and_4_out, not_13_out, not_14_out, not_15_out, IR_out_3[4]);
  and and_5 (and_5_out, not_16_out, not_17_out, not_18_out, IR_out_3[5]);
  and and_6 (and_6_out, IR_out_3[7], IR_out_3[6]);
  equivalence equivalence_1 (.in_1(R1_out_3[7:0]), .in_2(R1_out_3[15:8]), .out_3(equivalence_1_out_3));
  or or_5 (or_5_out, decoder_1_out12[6], decoder_1_out12[5]);
  and and_7 (and_7_out, not_19_out, not_20_out, IR_out_3[0], not_21_out, not_22_out);
  or or_6 (or_6_out, decoder_1_out12[6], decoder_1_out12[5], decoder_1_out12[4]);
  and and_8 (and_8_out, not_23_out, not_24_out, IR_out_3[5], IR_out_3[4]);
  or or_7 (or_7_out, decoder_1_out12[6], decoder_1_out12[5], decoder_1_out12[4]);
  and and_9 (and_9_out, PCtoMAR, clk);
  // Probe on MAR_out_3
  and and_10 (and_10_out, or_3_out, clk);
  // Probe on MBR_out_3
  and and_11 (and_11_out, CPUBUStoR1, clk);
  // Probe on R1_out_3[7:0]
  and and_12 (and_12_out, CPUBUStoR2, clk);
  // Probe on R1_out_3[15:8]
  and and_13 (and_13_out, MBRtoIR, clk);
  // Probe on IR_out_3
  Decoder #(.select(4)) decoder_1 (
    .out0(decoder_1_out0), .out1(decoder_1_out1), .out2(decoder_1_out2), .out3(decoder_1_out3),
    .out4(decoder_1_out4), .out5(decoder_1_out5), .out6(decoder_1_out12[6]), .out7(decoder_1_out12[5]),
    .out8(decoder_1_out12[4]), .out9(decoder_1_out12[3]), .out10(decoder_1_out12[2]),
    .out11(decoder_1_out12[1]), .out12(decoder_1_out12[0]), .out13(decoder_1_out13),
    .sel(jkcounter4bit_1_countoutput));  // open: out14, out15, en
  not not_25 (not_25_out, IR_out_3[1]);
  not not_26 (not_26_out, IR_out_3[1]);
  not not_27 (not_27_out, IR_out_3[0]);
  not not_28 (not_28_out, IR_out_3[5]);
  and and_14 (and_14_out, not_28_out, equivalence_1_out_3);
  and and_15 (and_15_out, IR_out_3[5], not_29_out);
  not not_29 (not_29_out, equivalence_1_out_3);
  not not_30 (not_30_out, IR_out_3[1]);
  not not_31 (not_31_out, IR_out_3[1]);
  and and_16 (and_16_out, not_32_out, nand_1_out);
  gate gate_7 (.in_2(and_27_out), .in_1({undriven_2, IR_out_3[3:0]}), .out_3(gate_7_out_3));
  gate gate_8 (.in_2(and_28_out), .in_1({undriven_3, IR_out_3[3:0]}), .out_3(gate_8_out_3));
  and and_17 (and_17_out, and_5_out, not_25_out, decoder_1_out12[6]);
  and and_18 (and_18_out, and_5_out, IR_out_3[1], decoder_1_out12[6]);
  and and_19 (and_19_out, and_5_out, not_26_out, decoder_1_out12[4]);
  and and_20 (and_20_out, and_5_out, IR_out_3[1], decoder_1_out12[4]);
  and and_21 (and_21_out, and_5_out, not_27_out, or_2_out);
  and and_22 (and_22_out, and_5_out, IR_out_3[0], or_2_out);
  or or_8 (or_8_out, and_14_out, and_15_out);
  and and_23 (and_23_out, and_7_out, not_30_out, or_6_out);
  and and_24 (and_24_out, and_7_out, IR_out_3[1], or_6_out);
  and and_25 (and_25_out, and_8_out, not_31_out, or_7_out);
  and and_26 (and_26_out, and_8_out, IR_out_3[1], or_7_out);
  gate gate_9 (.in_2(MARtoCPUBUS), .in_1(MAR_out_3), .out_3(gate_9_out_3));
  gate gate_10 (.in_2(MBRtoCPUBUS), .in_1(MBR_out_3), .out_3(gate_10_out_3));
  gate gate_11 (.in_2(R1toCPUBUS), .in_1(R1_out_3[7:0]), .out_3(gate_11_out_3));
  gate gate_12 (.in_2(R2toCPUBUS), .in_1(R1_out_3[15:8]), .out_3(gate_12_out_3));
  and and_27 (and_27_out, and_2_out, decoder_1_out12[6]);
  and and_28 (and_28_out, and_3_out, decoder_1_out12[3]);
  and and_29 (and_29_out, and_4_out, decoder_1_out12[6]);
  and and_30 (and_30_out, and_4_out, decoder_1_out12[5]);
  and and_31 (branch, or_8_out, and_6_out);
  gate gate_13 (.in_2(and_6_out), .in_1({undriven, IR_out_3[3:0]}), .out_3(branchadd));
  and and_32 (and_32_out, and_6_out, or_5_out);
  and and_33 (INPtoBUS, and_7_out, or_6_out);
  and and_34 (BUStoPRINT, and_8_out, or_7_out);
  // Probe on or_13_out
  or or_9 (or_9_out, decoder_1_out12[6], decoder_1_out12[5], decoder_1_out12[4]);
  or or_10 (or_10_out, decoder_1_out12[3], decoder_1_out12[2], decoder_1_out12[1]);
  or or_11 (or_11_out, decoder_1_out12[6], decoder_1_out12[5], decoder_1_out12[4]);
  or or_12 (or_12_out, decoder_1_out12[3], decoder_1_out12[2]);
  assign or_13_out = gate_14_out_3 | gate_9_out_3 | gate_10_out_3 | gate_12_out_3 | or_1_out | gate_11_out_3;  // OR_Gate or_13, 8 bits wide
  and and_35 (and_35_out, and_2_out, or_9_out);
  and and_36 (and_36_out, and_2_out, or_10_out);
  and and_37 (and_37_out, and_3_out, or_11_out);
  and and_38 (and_38_out, and_3_out, or_12_out);
  and and_39 (and_39_out, and_3_out, decoder_1_out12[1]);
  and and_40 (and_40_out, branch, and_32_out);
  gate gate_14 (.in_2(ALUtoCPUBUS), .in_1(mainalu_1_result), .out_3(gate_14_out_3));
  gate gate_15 (.in_2(CPUBUStoALUL), .in_1(or_13_out), .out_3(gate_15_out_3));
  gate gate_16 (.in_2(CPUBUStoALUR), .in_1(or_13_out), .out_3(gate_16_out_3));
  or or_14 (or_14_out, decoder_1_out1, decoder_1_out2);
  or or_15 (or_15_out, decoder_1_out4, decoder_1_out5);
  and and_41 (and_41_out, CPUBUStoALUL, clk);
  dRegister L (.in_2(gate_15_out_3), .out_3(L_out_3), .in_1(and_41_out));
  and and_42 (and_42_out, CPUBUStoALUR, clk);
  dRegister R (.in_2(gate_16_out_3), .out_3(R_out_3), .in_1(and_42_out));
  // Probe on L_out_3
  // Probe on R_out_3
  gate gate_17 (.in_2(MARtoBUS), .in_1(MAR_out_3), .out_3(gate_17_out_3));
  gate gate_18 (.in_2(MBRtoBUS), .in_1(MBR_out_3), .out_3(gate_18_out_3));
  mainALU mainalu_1 (
    .A(L_out_3), .B(R_out_3), .Overflow(mainalu_1_overflow), .Result(mainalu_1_result), .addOrSub(ADDSUB),
    .andOr(ALUandOr), .mathOrLogic(ALUmathlogic));  // open: Carry, Zero, Negative
  or or_16 (PCtoMAR, in_2, decoder_1_out0);
  or or_17 (PCplus1, in_7, decoder_1_out1, and_40_out);
  buf or_18 (MARtoCPUBUS, in_12);  // OR_Gate
  or or_19 (MARtoBUS, in_17, or_14_out);
  // Probe on gate_18_out_3
  // Probe on mainalu_1_result
  not not_32 (not_32_out, mainalu_1_overflow);
  assign or_20_out = gate_18_out_3 | gate_17_out_3 | gate_26_out_3 | gate_27_out_3;  // OR_Gate or_20, 8 bits wide
  assign or_21_out = or_20_out | gate_21_out_3;  // OR_Gate or_21, 8 bits wide
  gate gate_19 (.in_2(BUStoAR), .in_1(or_20_out), .out_3(gate_19_out_3));
  gate gate_20 (.in_2(DRINPUT), .in_1(or_21_out), .out_3(gate_20_out_3));
  gate gate_21 (.in_2(RAMtoDR), .in_1(ram16byte_1_out_5), .out_3(gate_21_out_3));
  Button b1 (.out(b1_out));
  Button b2 (.out(b2_out));
  Button b4 (.out(b4_out));
  Button b5 (.out(b5_out));
  Button b7 (.out(b7_out));
  Button b8 (.out(b8_out));
  Button zeroreset (.out(zeroreset_out));
  ROM16byte Rom (.out_3(Rom_out_3), .in_1(ROMINPUT), .out_2(Rom_out_2));
  and and_43 (and_43_out, clk, BUStoAR);
  dRegister AR (.in_2(gate_19_out_3), .out_3(AR_out_3), .in_1(and_43_out));
  and and_44 (and_44_out, clk, DRINPUT);
  dRegister DR (.in_2(gate_20_out_3), .out_3(DR_out_3), .in_1(and_44_out));
  // Probe on or_20_out
  Button b3 (.out(b3_out));
  Button b6 (.out(b6_out));
  Button b9 (.out(b9_out));
  // Probe on AR_out_3
  // Probe on DR_out_3
  gate gate_22 (.in_2(ROMtoRAM), .in_1(Rom_out_3), .out_3(gate_22_out_3));
  gate gate_23 (.in_2(ROMtoRAM), .in_1({undriven_4, Rom_out_2}), .out_3(gate_23_out_3));
  gate gate_24 (.in_2(ARtoRAM), .in_1(AR_out_3), .out_3(gate_24_out_3));
  gate gate_25 (.in_2(RWBIT), .in_1(DR_out_3), .out_3(gate_25_out_3));
  gate gate_26 (.in_2(DRtoBUS), .in_1(DR_out_3), .out_3(gate_26_out_3));
  keyboardwBuffer keyboardwbuffer_1 (
    .button2(b1_out), .b2(b2_out), .b3(b3_out), .b4(b4_out), .b5(b5_out), .b6(b6_out), .b7(b7_out),
    .b8(b8_out), .b9(b9_out), .reset(zeroreset_out), .out_11(keyboardwbuffer_1_out_11));
  or or_22 (RWBIT, in_3, ROMtoRAM, and_39_out);
  or or_23 (ARtoRAM, in_8, or_14_out, decoder_1_out3, and_35_out, and_39_out);
  or or_24 (DRINPUT, in_13, decoder_1_out3, and_35_out, and_37_out);
  or or_25 (DRtoBUS, in_18, or_15_out, and_36_out);
  or or_26 (BUStoAR, in_21, or_14_out, and_35_out, and_38_out);
  or or_27 (RAMtoDR, in_24, and_35_out, decoder_1_out3);
  // Probe on keyboardwbuffer_1_out_11
  assign or_28_out = gate_22_out_3 | gate_25_out_3;  // OR_Gate or_28, 8 bits wide
  assign or_29_out = gate_23_out_3 | gate_24_out_3;  // OR_Gate or_29, 8 bits wide
  // Probe on ram16byte_1_out_5
  gate gate_27 (.in_2(INPtoBUS), .in_1(keyboardwbuffer_1_out_11), .out_3(gate_27_out_3));
  ram16byte ram16byte_1 (.in_1(or_28_out), .in_4(or_29_out[3:0]), .in_3(clk), .in_2(RWBIT), .out_5(ram16byte_1_out_5));
  gate gate_28 (.in_2(BUStoPRINT), .in_1(or_20_out), .out_3(gate_28_out_3));
  and and_45 (and_45_out, BUStoPRINT, clk);
  dRegister dregister_1 (.in_2(gate_28_out_3), .out_3(dregister_1_out_3), .in_1(and_45_out));
  or or_30 (CPUBUStoMBR, in_4, and_35_out, and_37_out, and_38_out, and_26_out, and_25_out);
  or or_31 (MBRtoCPUBUS, in_9, and_36_out, and_24_out, and_23_out);
  or or_32 (MBRtoIR, in_14, or_15_out);
  or or_33 (BUStoMBR, in_19, or_15_out, and_36_out, and_24_out, and_23_out);
  or or_34 (MBRtoBUS, in_22, and_35_out, and_37_out, and_38_out, and_26_out, and_25_out);
  // Probe on dregister_1_out_3
  and and_46 (and_46_out, not_33_out, decoder_1_out12[4], and_4_out);
  and and_47 (and_47_out, IR_out_3[0], decoder_1_out12[4], and_4_out);
  not not_33 (not_33_out, IR_out_3[0]);
  and and_48 (and_48_out, not_34_out, and_2_out, and_36_out);
  not not_34 (not_34_out, IR_out_3[4]);
  and and_49 (and_49_out, not_35_out, and_37_out, and_3_out);
  and and_50 (and_50_out, IR_out_3[4], and_2_out, and_36_out);
  not not_35 (not_35_out, IR_out_3[4]);
  and and_51 (and_51_out, decoder_1_out12[4], and_4_out);
  and and_52 (and_52_out, IR_out_3[4], and_37_out, and_3_out);
  or or_35 (R1toCPUBUS, in_1, and_49_out, and_30_out, and_17_out, and_20_out, and_25_out);
  or or_36 (CPUBUStoR1, in_6, and_48_out, and_46_out, and_21_out, and_23_out);
  or or_37 (R2toCPUBUS, in_11, and_52_out, and_29_out, and_18_out, and_19_out, and_26_out);
  or or_38 (CPUBUStoR2, in_16, and_50_out, and_47_out, and_22_out, and_24_out);
  or or_39 (ADDSUB, in_5, and_22_out, and_21_out);
  or or_40 (CPUBUStoALUL, in_10, and_29_out, and_17_out, and_18_out);
  buf or_41 (ALUandOr, in_15);  // OR_Gate
  buf or_42 (ALUmathlogic, in_20);  // OR_Gate
  or or_43 (CPUBUStoALUR, in_23, and_30_out, and_19_out, and_20_out);
  or or_44 (ALUtoCPUBUS, in_25, and_51_out, and_22_out, and_21_out);

  // Notes on the sheet:
  //   CONTROL UNIT
  //   MAIN CLOCK CYCLE
  //   LOAD
  //   STORE
  //   ADD
  //   SUB
  //   1 is R2-R1, 0 is R1-R2
  //   BRANCH
  //   INP
  //   PRINT
  //   STOP
  //   TO CPU BUS
  //   TICKS 1-6: FETCH
  //   R1 to L
  //   R2 to L
  //   R2 to R
  //   R1 to R
  //   Send to R1/R2
  //   INP -> R1
  //   INP -> R2
  //   R1 -> OUT
  //   R2 -> OUT
  //   CPU bus
  //   7-13 INSTRUCTION
  //   PC/MAR GATES
  //   SysBus
  //   RAM GATES
  //   MBR GATES
  //   REGISTER GATES
  //   ALU GATES
endmodule

module ROM16byte (
  input  [3:0] in_1,
  output [3:0] out_2,
  output [7:0] out_3
);

  wire decoder_1_out0, decoder_1_out1, decoder_1_out2, decoder_1_out3, decoder_1_out4, decoder_1_out5,
       decoder_1_out6, decoder_1_out7, decoder_1_out8, decoder_1_out9, decoder_1_out10, decoder_1_out11,
       decoder_1_out12, decoder_1_out13, decoder_1_out14, decoder_1_out15;
  wire [4:4] not_4_out;
  wire [6:6] not_3_out;
  wire [7:0] gate_1_out_3, gate_2_out_3, gate_3_out_3, gate_4_out_3, gate_5_out_3, gate_6_out_3,
       gate_7_out_3, gate_8_out_3, gate_9_out_3, gate_10_out_3, gate_11_out_3, gate_12_out_3, gate_13_out_3,
       gate_14_out_3, gate_15_out_3, gate_16_out_3, or_1_out, or_2_out, or_3_out, or_4_out;
  wire [7:7] not_1_out, not_2_out;

  Decoder #(.select(4)) decoder_1 (
    .out0(decoder_1_out0), .out1(decoder_1_out1), .out2(decoder_1_out2), .out3(decoder_1_out3),
    .out4(decoder_1_out4), .out5(decoder_1_out5), .out6(decoder_1_out6), .out7(decoder_1_out7),
    .out8(decoder_1_out8), .out9(decoder_1_out9), .out10(decoder_1_out10), .out11(decoder_1_out11),
    .out12(decoder_1_out12), .out13(decoder_1_out13), .out14(decoder_1_out14), .out15(decoder_1_out15),
    .sel(in_1));  // open: en
  not not_1 (not_1_out[7], 1'b1);
  gate gate_1 (.in_2(decoder_1_out0), .in_1({{7{not_1_out[7]}}, 1'b1}), .out_3(gate_1_out_3));
  gate gate_2 (.in_2(decoder_1_out1), .in_1({1'b1, not_1_out[7], 1'b1, {4{not_1_out[7]}}, 1'b1}), .out_3(gate_2_out_3));
  gate gate_3 (.in_2(decoder_1_out2), .in_1({1'b1, {6{not_1_out[7]}}, 1'b1}), .out_3(gate_3_out_3));
  gate gate_4 (.in_2(decoder_1_out3), .in_1({1'b1, {2{not_1_out[7]}}, {5{1'b1}}}), .out_3(gate_4_out_3));
  assign or_1_out = gate_4_out_3 | gate_3_out_3 | gate_2_out_3 | gate_1_out_3;  // OR_Gate or_1, 8 bits wide
  not not_2 (not_2_out[7], 1'b1);
  gate gate_5 (.in_2(decoder_1_out4), .in_1({{3{not_2_out[7]}}, 1'b1, {3{not_2_out[7]}}, 1'b1}), .out_3(gate_5_out_3));
  gate gate_6 (.in_2(decoder_1_out5), .in_1({1'b1, not_2_out[7], {6{1'b1}}}), .out_3(gate_6_out_3));
  gate gate_7 (
    .in_2(decoder_1_out6), .in_1({{2{not_2_out[7]}}, 2'b11, {2{not_2_out[7]}}, 1'b1, not_2_out[7]}),
    .out_3(gate_7_out_3));
  gate gate_8 (.in_2(decoder_1_out7), .in_1({1'b1, {2{not_2_out[7]}}, 4'b1111, not_2_out[7]}), .out_3(gate_8_out_3));
  assign or_2_out = gate_8_out_3 | gate_7_out_3 | gate_6_out_3 | gate_5_out_3;  // OR_Gate or_2, 8 bits wide
  not not_3 (not_3_out[6], 1'b1);
  gate gate_9 (.in_2(decoder_1_out8), .in_1({1'b1, {7{not_3_out[6]}}}), .out_3(gate_9_out_3));
  gate gate_10 (
    .in_2(decoder_1_out9), .in_1({{2{not_3_out[6]}}, 1'b1, {3{not_3_out[6]}}, 2'b11}), .out_3(gate_10_out_3));
  gate gate_11 (
    .in_2(decoder_1_out10), .in_1({1'b1, {3{not_3_out[6]}}, 2'b11, not_3_out[6], 1'b1}), .out_3(gate_11_out_3));
  gate gate_12 (.in_2(decoder_1_out11), .in_1({1'b1, not_3_out[6], {5{1'b1}}, not_3_out[6]}), .out_3(gate_12_out_3));
  assign or_3_out = gate_12_out_3 | gate_11_out_3 | gate_10_out_3 | gate_9_out_3;  // OR_Gate or_3, 8 bits wide
  not not_4 (not_4_out[4], 1'b1);
  gate gate_13 (.in_2(decoder_1_out12), .in_1({3'b111, {3{not_4_out[4]}}, 1'b1, not_4_out[4]}), .out_3(gate_13_out_3));
  gate gate_14 (.in_2(decoder_1_out13), .in_1({8{not_4_out[4]}}), .out_3(gate_14_out_3));
  gate gate_15 (.in_2(decoder_1_out14), .in_1({{6{not_4_out[4]}}, 2'b11}), .out_3(gate_15_out_3));
  gate gate_16 (.in_2(decoder_1_out15), .in_1({8{not_4_out[4]}}), .out_3(gate_16_out_3));
  assign or_4_out = gate_16_out_3 | gate_15_out_3 | gate_14_out_3 | gate_13_out_3;  // OR_Gate or_4, 8 bits wide
  assign out_3 = or_4_out | or_3_out | or_2_out | or_1_out;  // OR_Gate or_5, 8 bits wide

  assign out_2 = in_1;

  // Notes on the sheet:
  //   ADDRESS 0000 TO 0011
  //   ADDRESS 0100 TO 0111
  //   ADDRESS 1000 TO 1011
  //   ADDRESS 1100 TO 1111
endmodule

module add1 (
  input  [7:0] in_1,
  output [7:0] out_2
);

  wire add_1bit_1_cout, add_1bit_2_cout, add_1bit_3_cout, add_1bit_4_cout, add_1bit_5_cout, add_1bit_6_cout,
       halfadder_1bit_1_carry_bit;

  HalfAdder_1bit halfadder_1bit_1 (.A(in_1[0]), .B(1'b1), .Sum_Bit(out_2[0]), .Carry_Bit(halfadder_1bit_1_carry_bit));
  Add_1Bit add_1bit_1 (
    .Sum(out_2[1]), .A(in_1[1]), .Cout(add_1bit_1_cout), .Cin(halfadder_1bit_1_carry_bit));  // open: B
  Add_1Bit add_1bit_2 (.Sum(out_2[2]), .A(in_1[2]), .Cout(add_1bit_2_cout), .Cin(add_1bit_1_cout));  // open: B
  Add_1Bit add_1bit_3 (.Sum(out_2[3]), .A(in_1[3]), .Cout(add_1bit_3_cout), .Cin(add_1bit_2_cout));  // open: B
  Add_1Bit add_1bit_4 (.Sum(out_2[4]), .A(in_1[4]), .Cout(add_1bit_4_cout), .Cin(add_1bit_3_cout));  // open: B
  Add_1Bit add_1bit_5 (.Sum(out_2[5]), .A(in_1[5]), .Cout(add_1bit_5_cout), .Cin(add_1bit_4_cout));  // open: B
  Add_1Bit add_1bit_6 (.Sum(out_2[6]), .A(in_1[6]), .Cout(add_1bit_6_cout), .Cin(add_1bit_5_cout));  // open: B
  Add_1Bit add_1bit_7 (.Sum(out_2[7]), .A(in_1[7]), .Cin(add_1bit_6_cout));  // open: B, Cout
endmodule

module gate (
  input  [7:0] in_1,
  input  in_2,
  output [7:0] out_3
);

  assign out_3 = in_1 & {8{in_2}};  // AND_Gate and_1, 8 bits wide
endmodule

module ROMDump (
  input  in_1,
  output [3:0] out_2,
  output out_3
);

  wire and_1_out, and_2_out, d_ff_1_qn, not_1_out, not_2_out, not_3_out, not_4_out;
  wire [4:0] jkcounter5bit_1_dataout;
  wire [7:4] dregister_1_out_3, undriven;

  not not_1 (not_1_out, in_1);
  and and_1 (and_1_out, not_1_out, d_ff_1_qn);
  jkcounter5bit jkcounter5bit_1 (.clk(and_1_out), .dataout(jkcounter5bit_1_dataout));  // open: reset
  not not_2 (not_2_out, jkcounter5bit_1_dataout[1]);
  not not_3 (not_3_out, jkcounter5bit_1_dataout[2]);
  not not_4 (not_4_out, jkcounter5bit_1_dataout[3]);
  and and_2 (and_2_out, jkcounter5bit_1_dataout[4], not_4_out, not_3_out, not_2_out, jkcounter5bit_1_dataout[0]);
  D_Flip_Flop d_ff_1 (.D(and_2_out), .clk(in_1), .Q(out_3), .Qn(d_ff_1_qn));  // open: preset, reset
  dRegister dregister_1 (
    .in_2({undriven, jkcounter5bit_1_dataout[3:0]}), .out_3({dregister_1_out_3, out_2}), .in_1(in_1));
endmodule

module jkcounter5bit (
  input  clk,
  input  reset,
  output [4:0] dataout
);

  wire and_1_out, and_2_out, and_3_out;

  J_K_Flip_Flop j_k_ff_1 (.J(1'b1), .K(1'b1), .clk(clk), .Q(dataout[0]), .reset(reset));  // open: Qn, preset
  J_K_Flip_Flop j_k_ff_2 (
    .J(dataout[0]), .K(dataout[0]), .clk(clk), .Q(dataout[1]), .reset(reset));  // open: Qn, preset
  and and_1 (and_1_out, dataout[0], dataout[1]);
  J_K_Flip_Flop j_k_ff_3 (.J(and_1_out), .K(and_1_out), .clk(clk), .Q(dataout[2]), .reset(reset));  // open: Qn, preset
  J_K_Flip_Flop j_k_ff_4 (.J(and_2_out), .K(and_2_out), .clk(clk), .Q(dataout[3]), .reset(reset));  // open: Qn, preset
  and and_2 (and_2_out, and_1_out, dataout[2]);
  and and_3 (and_3_out, and_2_out, dataout[3]);
  J_K_Flip_Flop j_k_ff_5 (.J(and_3_out), .K(and_3_out), .clk(clk), .Q(dataout[4]), .reset(reset));  // open: Qn, preset
endmodule

module equivalence (
  input  [7:0] in_1,
  input  [7:0] in_2,
  output out_3
);

  wire [7:0] xnor_1_out;

  assign xnor_1_out = ~(in_1 ^ in_2);  // XNOR_Gate xnor_1, 8 bits wide
  and and_1 (out_3, xnor_1_out[0], xnor_1_out[1], xnor_1_out[2], xnor_1_out[3], xnor_1_out[4], xnor_1_out[5], xnor_1_out[6], xnor_1_out[7]);
endmodule
